// Logisim project Stack_boundery_issue.circ as structural Verilog: 2 circuits, main circuit main
module main (
  input  RESET,
  input  pop,
  input  PUSH,
  input  [7:0] data_in,
  output Empty,
  output FULL,
  output [7:0] data_out
);

  wire and_1_out, and_2_out, clock_1_out, clock_2_out, clock_3_out, d_ff_1_q, multiplexer_1_out, not_1_out,
       not_2_out, pop_pulse_pulse, push_pulse_pulse;
  wire [1:0] counter_1_q;

  not not_1 (not_1_out, Empty);
  not not_2 (not_2_out, FULL);
  and and_1 (and_1_out, not_1_out, pop);
  and and_2 (and_2_out, not_2_out, PUSH);
  pulse_generator pop_pulse (.sig(and_1_out), .Pulse(pop_pulse_pulse));
  pulse_generator push_pulse (.sig(and_2_out), .Pulse(push_pulse_pulse));
  Multiplexer multiplexer_1 (
    .in0(pop_pulse_pulse), .in1(push_pulse_pulse), .out(multiplexer_1_out), .sel(push_pulse_pulse));
  Clock clock_1 (.out(clock_1_out));
  Counter #(.max('h3), .ongoal("stay"), .width(2)) counter_1 (
    .clr(RESET), .up(PUSH), .count(multiplexer_1_out), .clk(clock_2_out), .Q(counter_1_q));  // open: load, D, carry
  Clock clock_2 (.out(clock_2_out));
  D_Flip_Flop d_ff_1 (.D(pop_pulse_pulse), .clk(clock_1_out), .Q(d_ff_1_q));  // open: Qn, preset, reset
  Clock clock_3 (.out(clock_3_out));
  RAM #(.addrWidth(2)) ram_1 (
    .addr(counter_1_q), .we(push_pulse_pulse), .oe(d_ff_1_q), .clk(clock_3_out), .din(data_in),
    .dout(data_out));
  Comparator #(.width(2)) comparator_1 (.a(2'b00), .b(counter_1_q), .eq(Empty));  // open: gt, lt
  Comparator #(.width(2)) comparator_2 (.a(2'b11), .b(counter_1_q), .eq(FULL));  // open: gt, lt
endmodule

module pulse_generator (
  input  sig,
  output Pulse
);

  wire pulse_generator_CLK_out, pulse_generator_FF_q, xor_1_out;

  D_Flip_Flop pulse_generator_FF (
    .D(sig), .clk(pulse_generator_CLK_out), .Q(pulse_generator_FF_q));  // open: Qn, preset, reset
  Clock pulse_generator_CLK (.out(pulse_generator_CLK_out));
  xor xor_1 (xor_1_out, pulse_generator_FF_q, sig);
  and and_1 (Pulse, sig, xor_1_out);
endmodule
