// Logisim project Stack_no_full_or_empty.circ as structural Verilog: 2 circuits, main circuit main
module main (
  input  RESET,
  input  pop,
  input  PUSH,
  input  [7:0] data_in,
  output [1:0] ADDR_OUT,
  output [7:0] data_out
);

  wire clock_1_out, clock_2_out, multiplexer_1_out, pulse_generator_1_pulse, pulse_generator_2_pulse;

  pulse_generator pulse_generator_1 (.sig(pop), .Pulse(pulse_generator_1_pulse));
  pulse_generator pulse_generator_2 (.sig(PUSH), .Pulse(pulse_generator_2_pulse));
  Multiplexer multiplexer_1 (
    .in0(pulse_generator_1_pulse), .in1(pulse_generator_2_pulse), .out(multiplexer_1_out),
    .sel(pulse_generator_2_pulse));
  Counter #(.max('h3), .ongoal("stay"), .width(2)) counter_1 (
    .clr(RESET), .up(PUSH), .count(multiplexer_1_out), .clk(clock_1_out), .Q(ADDR_OUT));  // open: load, D, carry
  Clock clock_1 (.out(clock_1_out));
  Clock clock_2 (.out(clock_2_out));
  RAM #(.addrWidth(2)) ram_1 (
    .addr(ADDR_OUT), .we(pulse_generator_2_pulse), .oe(pulse_generator_1_pulse), .clk(clock_2_out),
    .din(data_in), .dout(data_out));
  // Probe on nothing
endmodule

module pulse_generator (
  input  sig,
  output Pulse
);

  wire pulse_generator_CLK_out, pulse_generator_FF_q, xor_1_out;

  D_Flip_Flop pulse_generator_FF (
    .D(sig), .clk(pulse_generator_CLK_out), .Q(pulse_generator_FF_q));  // open: Qn, preset, reset
  Clock pulse_generator_CLK (.out(pulse_generator_CLK_out));
  xor xor_1 (xor_1_out, pulse_generator_FF_q, sig);
  and and_1 (Pulse, sig, xor_1_out);
endmodule
