// Logisim project working_Stack_v2.circ as structural Verilog: 2 circuits, main circuit main
module main (
  input  RESET,
  input  pop,
  input  PUSH,
  input  [7:0] data_in,
  output Empty,
  output FULL,
  output [7:0] data_out
);

  wire and_1_out, and_2_out, clock_1_out, clock_2_out, clock_3_out, clock_4_out, flip_flop_d_q, not_1_out,
       not_2_out, or_1_out, pop_pulse_pulse, push_pulse_pulse;
  wire [1:0] counter_1_q;
  wire [7:0] RAM_1_dout;

  pulse_generator pop_pulse (.sig(pop), .Pulse(pop_pulse_pulse));
  pulse_generator push_pulse (.sig(PUSH), .Pulse(push_pulse_pulse));
  not not_1 (not_1_out, Empty);
  not not_2 (not_2_out, FULL);
  and and_1 (and_1_out, not_1_out, pop_pulse_pulse);
  and and_2 (and_2_out, not_2_out, push_pulse_pulse);
  or or_1 (or_1_out, and_2_out, and_1_out);
  Clock clock_1 (.out(clock_1_out));
  Counter #(.max('h3), .ongoal("stay"), .width(2)) counter_1 (
    .clr(RESET), .up(and_2_out), .count(or_1_out), .clk(clock_2_out), .Q(counter_1_q));  // open: load, D, carry
  Clock clock_2 (.out(clock_2_out));
  D_Flip_Flop flip_flop_d (.D(and_1_out), .clk(clock_1_out), .Q(flip_flop_d_q));  // open: Qn, preset, reset
  Clock clock_3 (.out(clock_3_out));
  RAM #(.addrWidth(2)) RAM_1 (
    .addr(counter_1_q), .we(and_2_out), .oe(flip_flop_d_q), .clk(clock_3_out), .din(data_in),
    .dout(RAM_1_dout));
  Comparator #(.width(2)) comparator_1 (.a(2'b00), .b(counter_1_q), .eq(Empty));  // open: gt, lt
  Comparator #(.width(2)) comparator_2 (.a(2'b11), .b(counter_1_q), .eq(FULL));  // open: gt, lt
  Clock clock_4 (.out(clock_4_out));
  Register output_register (.D(RAM_1_dout), .en(pop), .clk(clock_4_out), .Q(data_out), .clr(RESET));
endmodule

module pulse_generator (
  input  sig,
  output Pulse
);

  wire pulse_generator_CLK_out, pulse_generator_FF_q, xor_1_out;

  D_Flip_Flop pulse_generator_FF (
    .D(sig), .clk(pulse_generator_CLK_out), .Q(pulse_generator_FF_q));  // open: Qn, preset, reset
  Clock pulse_generator_CLK (.out(pulse_generator_CLK_out));
  xor xor_1 (xor_1_out, pulse_generator_FF_q, sig);
  and and_1 (Pulse, sig, xor_1_out);
endmodule
